// Logisim project Lift Control [FINAL].circ as structural Verilog: 1 circuit, main circuit main
module main (
  input  [2:0] D_E_F,
  input  A,
  input  [2:0] GND,
  input  W_1,
  input  W_2
);

  wire multiplexer_1_out, multiplexer_3_out, multiplexer_4_out, multiplexer_5_out, multiplexer_6_out,
       multiplexer_8_out, multiplexer_9_out, multiplexer_10_out, nor_1_out, not_1_out, not_2_out, not_3_out;

  not not_1 (not_1_out, W_1);
  not not_2 (not_2_out, W_2);
  not not_3 (not_3_out, A);
  nor nor_1 (nor_1_out, W_1, W_2);
  Multiplexer #(.select(3), .enable("false")) multiplexer_1 (
    .in0(not_3_out), .in1(1'b1), .in2(1'b1), .in3(1'b1), .in4(not_3_out), .in5(1'b0), .in6(A), .in7(A),
    .out(multiplexer_1_out), .sel(D_E_F));
  Multiplexer #(.select(3)) multiplexer_2 (
    .in0(multiplexer_1_out), .in1(multiplexer_3_out), .in2(multiplexer_5_out), .in3(multiplexer_9_out),
    .in4(1'b0), .in5(1'b0), .in6(1'b0), .in7(1'b0), .out(not_1_out), .sel(GND), .en(nor_1_out));
  Multiplexer #(.select(3), .enable("false")) multiplexer_3 (
    .in0(1'b1), .in1(1'b1), .in2(A), .in3(A), .in4(1'b1), .in5(1'b1), .in6(A), .in7(1'b0),
    .out(multiplexer_3_out), .sel(D_E_F));
  Multiplexer #(.select(3), .enable("false")) multiplexer_4 (
    .in0(A), .in1(1'b0), .in2(1'b0), .in3(1'b0), .in4(A), .in5(1'b1), .in6(not_3_out), .in7(not_3_out),
    .out(multiplexer_4_out), .sel(D_E_F));
  LED Lift_A (.in(not_1_out));
  LED Lift_B (.in(not_2_out));
  Multiplexer #(.select(3), .enable("false")) multiplexer_5 (
    .in0(1'b0), .in1(not_3_out), .in2(1'b1), .in3(1'b1), .in4(not_3_out), .in5(not_3_out), .in6(1'b1),
    .in7(1'b1), .out(multiplexer_5_out), .sel(D_E_F));
  Multiplexer #(.select(3), .enable("false")) multiplexer_6 (
    .in0(1'b0), .in1(1'b0), .in2(not_3_out), .in3(not_3_out), .in4(1'b0), .in5(1'b0), .in6(not_3_out),
    .in7(1'b1), .out(multiplexer_6_out), .sel(D_E_F));
  Multiplexer #(.select(3)) multiplexer_7 (
    .in0(multiplexer_4_out), .in1(multiplexer_6_out), .in2(multiplexer_8_out), .in3(multiplexer_10_out),
    .in4(1'b0), .in5(1'b0), .in6(1'b0), .in7(1'b0), .out(not_2_out), .sel(GND), .en(nor_1_out));
  Multiplexer #(.select(3), .enable("false")) multiplexer_8 (
    .in0(1'b1), .in1(A), .in2(1'b0), .in3(1'b0), .in4(A), .in5(A), .in6(1'b0), .in7(1'b0),
    .out(multiplexer_8_out), .sel(D_E_F));
  Multiplexer #(.select(3), .enable("false")) multiplexer_9 (
    .in0(not_3_out), .in1(not_3_out), .in2(1'b0), .in3(A), .in4(1'b1), .in5(1'b1), .in6(1'b1), .in7(A),
    .out(multiplexer_9_out), .sel(D_E_F));
  Multiplexer #(.select(3), .enable("false")) multiplexer_10 (
    .in0(A), .in1(A), .in2(A), .in3(not_3_out), .in4(1'b0), .in5(1'b0), .in6(1'b0), .in7(not_3_out),
    .out(multiplexer_10_out), .sel(D_E_F));

  // Notes on the sheet:
  //      B C
  //     A1
  //   A5
  //   A2
  //   B1
  //   A3
  //   B2
  //   B5
  //   B3
  //   A4
  //   Legend
  //   A,B - Floor of Lift 1
  //   C,D - Floor of Lift 2
  //   E,F - Call Floor
  //   W(1) - Lift 1 is overloaded
  //   W(2) - Lift 2 is overloaded
  //   B4
endmodule
